// Logisim project 16-Bit-CPU.circ as structural Verilog: 1 circuit, main circuit main
module main (
  input  Clear_Global_Mem,
  input  in_2,
  input  Clear_IO_Mem
);

  wire ALU, ALUI, and_1_out, and_2_out, beq, button_1_out, button_2_out, button_3_out, button_4_out,
       button_5_out, button_6_out, button_7_out, button_8_out, clk, Clock_out, comparator_1_eq,
       comparator_1_lt, comparator_2_eq, copy, COPYSTD, decoder_2_out0, decoder_2_out1, decoder_2_out2,
       decoder_2_out3, decoder_3_out0, decoder_3_out1, decoder_3_out2, decoder_3_out3, decoder_4_out0,
       decoder_4_out1, decoder_4_out2, decoder_4_out3, decoder_5_out0, decoder_5_out1, decoder_5_out2,
       decoder_5_out3, decoder_6_out0, decoder_6_out1, decoder_6_out2, decoder_6_out3, halt, ISRJumpControl,
       jal, load, LoadJalRegisters, multiplexer_1_out, not_1_out, or_1_out, or_2_out, or_3_out, or_4_out,
       RALoad, RAReturn, ReadJalRegisters, register_1_q, register_2_q, register_3_q, register_4_q,
       register_5_q, register_6_q, register_7_q, register_10_q, RINT, store, storeGlobal, storeIO, tty,
       ttyALoad, ttyLoad;
  wire [1:0] loadDecode, SubopField;
  wire [2:0] ISRControl, ram_1_data, regField;
  wire [6:0] multiplexer_10_out;
  wire [7:0] accOut, adder_2_out, ALUOut, divider_1_out, globalOut, imm, ioOut, JALRegOut, multiplexer_2_out,
       multiplexer_7_out, multiplexer_9_out, multiplexer_11_out, multiplier_1_out, regOut, subtractor_1_out;
  wire [15:0] adder_1_out, bit_extender_1_out, INT_RET_REG, ISRVector, multiplexer_3_out, multiplexer_4_out,
       multiplexer_6_out, PCOut, ra_q, RAOut;

  Comparator comparator_1 (.a(regOut), .b(accOut), .eq(comparator_1_eq), .lt(comparator_1_lt));  // open: gt
  not not_1 (not_1_out, comparator_1_eq);
  Button button_1 (.out(button_1_out));
  Multiplexer #(.select(2), .enable("false")) multiplexer_1 (
    .in0(comparator_1_eq), .in1(not_1_out), .in2(comparator_1_lt), .out(multiplexer_1_out), .sel(SubopField));  // open: in3
  Comparator #(.width(2)) comparator_2 (.a(SubopField), .b(2'b11), .eq(comparator_2_eq));  // open: gt, lt
  Register #(.width(1)) register_1 (.D(button_1_out), .Q(register_1_q), .clk(button_1_out), .clr(clk));  // open: en
  Register #(.width(1)) register_2 (.D(button_2_out), .Q(register_2_q), .clk(button_2_out), .clr(clk));  // open: en
  Button button_2 (.out(button_2_out));
  assign bit_extender_1_out = {{8{imm[7]}}, imm};  // Bit_Extender bit_extender_1
  and and_1 (and_1_out, beq, multiplexer_1_out);
  or or_1 (or_1_out, and_1_out, and_2_out, RALoad);
  and and_2 (and_2_out, comparator_2_eq, beq);
  Multiplexer #(.width(8), .enable("false")) multiplexer_2 (
    .in0(imm), .in1(accOut), .out(multiplexer_2_out), .sel(ALU));
  // NOT_Gate not_2 has open pins: in=open, out=ISRJumpControl
  Register #(.width(1)) register_3 (.D(button_3_out), .Q(register_3_q), .clk(button_3_out), .clr(clk));  // open: en
  Button button_3 (.out(button_3_out));
  Button button_4 (.out(button_4_out));
  Adder #(.width(16)) adder_1 (.a(PCOut), .b(multiplexer_3_out), .out(adder_1_out));  // open: cin, cout
  Multiplexer #(.width(16), .enable("false")) multiplexer_3 (
    .in0(16'h1), .in1(bit_extender_1_out), .out(multiplexer_3_out), .sel(or_1_out));
  Adder adder_2 (.a(regOut), .b(multiplexer_2_out), .out(adder_2_out));  // open: cin, cout
  Subtractor subtractor_1 (.a(regOut), .b(multiplexer_2_out), .out(subtractor_1_out));  // open: bin, bout
  Multiplier multiplier_1 (.a(regOut), .b(multiplexer_2_out), .out(multiplier_1_out));  // open: cin, cout
  Divider divider_1 (.a(regOut), .b(multiplexer_2_out), .out(divider_1_out));  // open: upper, rem
  Priority_Encoder #(.disabled(0)) priority_encoder_1 (
    .in0(register_1_q), .in1(register_2_q), .in2(register_3_q), .in3(register_4_q), .in4(register_5_q),
    .in5(register_6_q), .in6(register_7_q), .in7(register_10_q), .out(ISRControl));  // open: en_in
  Register #(.width(1)) register_4 (.D(button_4_out), .Q(register_4_q), .clk(button_4_out), .clr(clk));  // open: en
  Button button_5 (.out(button_5_out));
  Multiplexer #(.select(2), .width(16), .enable("false")) multiplexer_4 (
    .in0(adder_1_out), .in1(RAOut), .in2(ISRVector), .out(multiplexer_4_out), .sel({ISRJumpControl, RAReturn}));  // open: in3
  Multiplexer #(.select(2), .width(8), .enable("false")) multiplexer_5 (
    .in0(adder_2_out), .in1(subtractor_1_out), .in2(multiplier_1_out), .in3(divider_1_out), .out(ALUOut),
    .sel(SubopField));
  ROM #(.addrWidth(3), .dataWidth(16)) rom_1 (.addr(ISRControl), .data(ISRVector));  // open: sel
  Register #(.width(1)) register_5 (.D(button_5_out), .Q(register_5_q), .clk(button_5_out), .clr(clk));  // open: en
  Register #(.width(1)) register_6 (.D(button_6_out), .Q(register_6_q), .clk(button_6_out), .clr(clk));  // open: en
  Button button_6 (.out(button_6_out));
  Multiplexer #(.width(16), .enable("false")) multiplexer_6 (
    .in0(multiplexer_4_out), .in1(INT_RET_REG), .out(multiplexer_6_out), .sel(RINT));
  Register #(.width(1)) register_7 (.D(button_8_out), .Q(register_7_q), .clk(button_8_out), .clr(clk));  // open: en
  Button button_7 (.out(button_7_out));
  Button button_8 (.out(button_8_out));
  Register #(.width(16)) register_8 (.D(multiplexer_6_out), .Q(PCOut), .clk(clk), .clr(in_2));  // open: en
  Register #(.width(16)) register_9 (.D(PCOut), .Q(INT_RET_REG), .clk(or_2_out), .clr(in_2));  // open: en
  or or_2 (or_2_out, register_1_q, register_2_q, register_3_q, register_4_q, register_5_q, register_6_q, register_7_q, register_10_q);
  Register #(.width(1)) register_10 (.D(button_7_out), .Q(register_10_q), .clk(button_7_out), .clr(clk));  // open: en
  RAM #(.addrWidth(16), .dataWidth(16), .bus("separate")) ram_1 (
    .addr(PCOut), .data({imm, SubopField, regField, ram_1_data}), .str(1'b0), .clk(clk));  // open: din, sel, ld, clr
  RAM #(.addrWidth(3), .bus("separate")) ram_2 (
    .addr(regField), .din(accOut), .data(regOut), .str(COPYSTD), .clk(clk), .clr(in_2));  // open: sel, ld
  RAM #(.bus("separate")) ram_3 (
    .addr(imm), .din(accOut), .data(globalOut), .str(storeGlobal), .clk(clk), .clr(Clear_Global_Mem));  // open: sel, ld
  RAM #(.bus("separate")) ram_4 (
    .addr(imm), .din(accOut), .data(ioOut), .str(storeIO), .clk(clk), .clr(Clear_IO_Mem));  // open: sel, ld
  Decoder #(.select(3), .enable("false")) decoder_1 (
    .out0(jal), .out1(ALUI), .out2(ALU), .out3(tty), .out4(copy), .out5(beq), .out6(load), .out7(store),
    .sel(ram_1_data));
  Decoder #(.select(2), .enable("false")) decoder_2 (
    .out0(decoder_2_out0), .out1(decoder_2_out1), .out2(decoder_2_out2), .out3(decoder_2_out3),
    .sel(SubopField));
  Decoder #(.select(2), .enable("false")) decoder_3 (
    .out0(decoder_3_out0), .out1(decoder_3_out1), .out2(decoder_3_out2), .out3(decoder_3_out3),
    .sel(SubopField));
  Multiplexer #(.select(2), .width(8), .enable("false")) multiplexer_7 (
    .in0(globalOut), .in2(ioOut), .out(multiplexer_7_out), .sel(loadDecode));  // open: in1, in3
  Clock Clock (.out(Clock_out));
  Multiplexer #(.enable("false")) multiplexer_8 (.in0(Clock_out), .in1(1'b0), .out(clk), .sel(halt));
  Multiplexer #(.width(8), .enable("false")) multiplexer_9 (
    .in0(ALUOut), .in1(multiplexer_7_out), .out(multiplexer_9_out), .sel(load));
  Multiplexer #(.width(7), .enable("false")) multiplexer_10 (
    .in0(imm[6:0]), .in1(accOut[6:0]), .out(multiplexer_10_out), .sel(imm[7]));
  TTY #(.rows(9)) tty_1 (.data(multiplexer_10_out), .clk(clk), .we(or_3_out), .clr(in_2));
  or or_3 (or_3_out, ttyLoad, ttyALoad);
  Multiplexer #(.width(8), .enable("false")) multiplexer_11 (
    .in0(multiplexer_9_out), .in1(JALRegOut), .out(multiplexer_11_out), .sel(ReadJalRegisters));
  and and_3 (storeGlobal, decoder_2_out0, store);
  and and_4 (storeIO, decoder_2_out1, store);
  // AND_Gate and_5 has open pins: in0=decoder_2_out2, in1=store, out=open
  // AND_Gate and_6 has open pins: in0=decoder_2_out3, in1=store, out=open
  and and_7 (loadDecode[0], decoder_3_out0, load);
  and and_8 (loadDecode[1], decoder_3_out1, load);
  // AND_Gate and_9 has open pins: in0=decoder_3_out2, in1=load, out=open
  // AND_Gate and_10 has open pins: in0=decoder_3_out3, in1=load, out=open
  or or_4 (or_4_out, ALUI, load, ALU, ReadJalRegisters);
  Decoder #(.select(2), .enable("false")) decoder_4 (
    .out0(decoder_4_out0), .out1(decoder_4_out1), .out2(decoder_4_out2), .out3(decoder_4_out3),
    .sel(SubopField));
  Decoder #(.select(2), .enable("false")) decoder_5 (
    .out0(decoder_5_out0), .out1(decoder_5_out1), .out2(decoder_5_out2), .out3(decoder_5_out3),
    .sel(SubopField));
  Register Accumulator (.D(multiplexer_11_out), .en(or_4_out), .Q(accOut), .clk(clk), .clr(in_2));
  and and_11 (COPYSTD, decoder_4_out0, copy);
  and and_12 (RINT, decoder_4_out1, copy);
  // AND_Gate and_13 has open pins: in0=decoder_4_out2, in1=copy, out=open
  // AND_Gate and_14 has open pins: in0=decoder_4_out3, in1=copy, out=open
  and and_15 (RALoad, decoder_5_out0, jal);
  and and_16 (RAReturn, decoder_5_out1, jal);
  and and_17 (LoadJalRegisters, decoder_5_out2, jal);
  and and_18 (ReadJalRegisters, decoder_5_out3, jal);
  Register #(.width(16)) ra (.D(PCOut), .en(RALoad), .Q(ra_q), .clk(clk), .clr(in_2));
  Decoder #(.select(2), .enable("false")) decoder_6 (
    .out0(decoder_6_out0), .out1(decoder_6_out1), .out2(decoder_6_out2), .out3(decoder_6_out3),
    .sel(SubopField));
  Adder #(.width(16)) adder_3 (.a(ra_q), .b(16'h1), .out(RAOut));  // open: cin, cout
  and and_19 (ttyLoad, decoder_6_out0, tty);
  and and_20 (ttyALoad, decoder_6_out1, tty);
  and and_21 (halt, decoder_6_out2, tty);
  // AND_Gate and_22 has open pins: in0=decoder_6_out3, in1=tty, out=open
  RAM #(.addrWidth(3), .bus("separate")) ram_5 (
    .addr(regField), .din(accOut), .data(JALRegOut), .str(LoadJalRegisters), .clk(clk), .clr(in_2));  // open: sel, ld

  // Other names for the same wires on the sheet: rst = in_2

  // Notes on the sheet:
  //   done
  //   done
  //   contents of rom_1 (hex, n*v repeats v):
  //   0 b 0 0 0 5
  //   done
  //   done
  //   done
  //   Instruction RAM
  //   Register File
  //   OP Code Logic
  //   Done
  //   done
  //   done
  //   done
  //   done
  //   done
endmodule
